# Fritzing sketch fritzing diagram (saved by Fritzing 0.9.6b)
breadboards: 1

parts:
  Part1 = Arduino Nano (Rev3.0)
  MQ2/SMOKE_sensor = MQ-4
  temp_sensor = Humidity and Temperature Sensor RHT03
  WATER_PUMP = DC Motor
  Q1 = NPN-Transistor [package="SOT-23 [SMD]"]
  R1 = Resistor [tolerance=±5% resistance=220 package="2512 [SMD]"]
  R2 = Resistor [tolerance=±5% resistance=220 package="2512 [SMD]"]
  9_V_SUPPLY = Power plug

nets:
  GND: Part1.GND, Q1.2, 9_V_SUPPLY.GND
  N1: Part1.D4, MQ2/SMOKE_sensor.DO
  N2: Part1.D8, temp_sensor.Data-signal, R2.Pin_0
  VIN: Part1.VIN, WATER_PUMP.pin_1, 9_V_SUPPLY.VCC
  VCC: Part1.5V, MQ2/SMOKE_sensor.VCC, temp_sensor.Vcc, R2.Pin_1
  N3: Part1.A6, MQ2/SMOKE_sensor.AO
  N4: Part1.A0, R1.Pin_1
  N5: MQ2/SMOKE_sensor.GND, temp_sensor.GND_2
  N6: WATER_PUMP.pin_2, Q1.1
  N7: Q1.0, R1.Pin_0
